// Logisim project Part4.circ as structural Verilog
module Ex4 (
  input  [7:0] IN1,
  output OUT1,
  output [7:0] OUT2
);

  and and_1 (OUT1, IN1[0], IN1[7]);

  assign OUT2 = IN1;

  // Other names for the same wires on the sheet: R0 = IN1[0]; R16[5:0] = IN1[6:1]; R7 = IN1[7]
endmodule
