// Logisim project part1.circ as structural Verilog
module NAND1 (
  input  IN1,
  input  IN2,
  output OUT1
);

  and and_1 (OUT1, IN1, IN2);
endmodule

module XOR1 (
  input  IN1,
  input  IN2,
  output OUT1
);

  wire and_1_out, and_2_out, not_1_out, not_2_out;

  not not_1 (not_1_out, IN2);
  not not_2 (not_2_out, IN1);
  and and_1 (and_1_out, IN1, not_1_out);
  and and_2 (and_2_out, not_2_out, IN2);
  or or_1 (OUT1, and_1_out, and_2_out);
endmodule

module MUX21 (
  input  S,
  input  IN1,
  input  IN2,
  output OUT1
);

  wire and_1_out, and_2_out, not_1_out;

  not not_1 (not_1_out, S);
  and and_1 (and_1_out, not_1_out, IN1);
  and and_2 (and_2_out, S, IN2);
  or or_1 (OUT1, and_1_out, and_2_out);
endmodule

module MUX41 (
  input  S1,
  input  S2,
  input  IN1,
  input  IN2,
  input  IN3,
  input  IN4,
  output OUT1
);

  wire and_1_out, and_2_out, and_3_out, and_4_out, and_5_out, and_6_out, and_7_out, and_8_out, not_1_out,
       not_2_out, or_1_out, or_2_out;

  not not_1 (not_1_out, S1);
  not not_2 (not_2_out, S2);
  and and_1 (and_1_out, not_1_out, not_2_out);
  and and_2 (and_2_out, S1, not_2_out);
  and and_3 (and_3_out, not_1_out, S2);
  and and_4 (and_4_out, S1, S2);
  and and_5 (and_5_out, and_1_out, IN1);
  and and_6 (and_6_out, and_2_out, IN2);
  and and_7 (and_7_out, and_3_out, IN3);
  and and_8 (and_8_out, and_4_out, IN4);
  or or_1 (or_1_out, and_5_out, and_6_out);
  or or_2 (or_2_out, and_7_out, and_8_out);
  or or_3 (OUT1, or_1_out, or_2_out);
endmodule
