// Logisim project part2.circ as structural Verilog: 2 circuits, main circuit main
module main (
  output [7:0] out_1,
  output [7:0] out_2
);

  AddMachine addmachine_1 (.IN1(out_1), .OUT1(out_2));
endmodule

module AddMachine (
  output [7:0] IN1,
  output [7:0] OUT1
);

  wire clock_1_out;

  Clock #(.highDuration(2), .lowDuration(2)) clock_1 (.out(clock_1_out));
  Adder adder_1 (.a(8'h1), .b(OUT1), .out(IN1));  // open: cin, cout
  Register register_1 (.D(IN1), .clk(clock_1_out), .Q(OUT1));  // open: en, clr
endmodule
